# Fritzing sketch Breadboard (saved by Fritzing 0.9.4)
breadboards: 1

parts:
  Part1 = Adafruit Trinket M0 [part_number="Adafruit #3500"]
  BUTTON1 = Arcade Button (green)
  BUTTON2 = Arcade Button (yellow)
  S2 = Taiway 100-SP-X-T1 SPDT Miniature Toggle Switch [part_number=100-SP-X-T1-0-0-B1-M2 package=THT]
  S3 = Taiway 100-SP-X-T1 SPDT Miniature Toggle Switch [part_number=100-SP-X-T1-0-0-B1-M2 package=THT]

nets:
  N1: Part1.GND, BUTTON1.no_name_yet#2, BUTTON2.no_name_yet#2, S2.L2, S3.L2
  N2: Part1.D4_A2_PA06_TXD_MOSI, BUTTON1.no_name_yet#1
  N3: Part1.D3_A3_PA07_RXD_SCK, BUTTON2.no_name_yet#1
  N4: Part1.D1_A0_PA02, S2.L1
  N5: Part1.D0_A4_PA08_SDA, S3.L1

custom parts:
  Arcade Button (green): Adafruit Arcade Button (green)
  Arcade Button (yellow): Adafruit Arcade Button (yellow)
